# Fritzing sketch blink (saved by Fritzing 0.9.5d)
circuit board: 8.46667cm x 5.64444cm
breadboards: 1

parts:
  U1 = NodeMCU V1.0
  LED1 = LED - 5mm [color="Red (633nm)" package="5 mm [THT]"]
  R1 = Resistor [tolerance=±0.5% resistance=220 package=THT]

nets:
  N1: U1.D2, LED1.anode
  N2: U1.GND, R1.Pin_0
  N3: LED1.cathode, R1.Pin_1

custom parts:
  NodeMCU V1.0: ESP9266 based NodeMCU
