# Fritzing sketch button (saved by Fritzing 0.9.5d)
circuit board: 8.46667cm x 5.64444cm
breadboards: 1

parts:
  U1 = NodeMCU V1.0
  LED1 = LED - 5mm [color="Red (633nm)" package="5 mm [THT]"]
  R1 = Resistor [tolerance=±0.5% resistance=220 package=THT]
  S1 = Pushbutton [package="[THT]"]
  R2 = Resistor [tolerance=±0.5% resistance=220 package=THT]

nets:
  N1: U1.D1, S1.Pin_3, S1.Pin_4, R2.Pin_1
  N2: U1.3V3, S1.Pin_1, S1.Pin_2
  N3: U1.GND, R1.Pin_0, R2.Pin_0
  N4: U1.D5, LED1.anode
  N5: LED1.cathode, R1.Pin_1

custom parts:
  NodeMCU V1.0: ESP8266 based NodeMCU
