# Fritzing sketch led_party (saved by Fritzing 0.9.5d)
circuit board: 8.46667cm x 5.64444cm
breadboards: 1

parts:
  U1 = NodeMCU V1.0
  LED1 = LED - 5mm [color="Red (633nm)" package="5 mm [THT]"]
  R1 = Resistor [tolerance=±0.5% resistance=220 package=THT]  # not connected
  LED2 = LED - 5mm [color="Yellow (595nm)" package="5 mm [THT]"]
  R2 = Resistor [tolerance=±0.5% resistance=220 package=THT]
  LED3 = LED - 5mm [color="Green (570nm)" package="5 mm [THT]"]
  R3 = Resistor [tolerance=±0.5% resistance=220 package=THT]
  LED4 = LED - 5mm [color="Blue (525nm)" package="5 mm [THT]"]
  R4 = Resistor [tolerance=±0.5% resistance=10k package=THT]
  S1 = Pushbutton [package="[SMD]"]
  R5 = Resistor [tolerance=±0.5% resistance=220 package=THT]

nets:
  N1: U1.D1, LED1.anode
  N2: U1.D2, LED2.anode
  N3: U1.D3, LED3.anode
  N4: U1.3V3, S1.Pin_1, S1.Pin_2
  N5: U1.GND, R2.Pin_0, R3.Pin_0, R4.Pin_0, R5.Pin_0
  N6: U1.D5, LED4.anode
  N7: U1.D6, S1.Pin_3, S1.Pin_4, R5.Pin_1
  N8: LED2.cathode, R2.Pin_1
  N9: LED3.cathode, R3.Pin_1
  N10: LED4.cathode, R4.Pin_1

notes:
  The resistor for the blue LED has a different value than the others (10k).

custom parts:
  NodeMCU V1.0: ESP8266 based NodeMCU
