# Fritzing sketch space_invaders (saved by Fritzing 0.9.5d)
breadboards: 1

parts:
  OLED1 = OLED 128x64 I2C Monochrome Display
  S1 = Pushbutton [package="[THT]"]
  S2 = Pushbutton [package="[THT]"]
  S3 = Pushbutton [package="[THT]"]
  U1 = NodeMCU V1.0
  R1 = Resistor [tolerance=±5% resistance=220 package=THT]
  R2 = Resistor [tolerance=±5% resistance=220 package=THT]
  R3 = Resistor [tolerance=±5% resistance=220 package=THT]

nets:
  GND: OLED1.GND, U1.GND, R1.Pin_1, R2.Pin_1, R3.Pin_1
  VDD: OLED1.VDD, S1.Pin_3, S1.Pin_4, S2.Pin_1, S2.Pin_2, S3.Pin_1, S3.Pin_2, U1.3V3
  N1: OLED1.SCK, U1.D4
  N2: OLED1.SDA, U1.D3
  N3: S1.Pin_1, S1.Pin_2, U1.D1, R1.Pin_0
  N4: S2.Pin_3, S2.Pin_4, U1.D5, R2.Pin_0
  N5: S3.Pin_3, S3.Pin_4, U1.D2, R3.Pin_0

custom parts:
  NodeMCU V1.0: ESP8266 based NodeMCU
