# Fritzing sketch sensor (saved by Fritzing 0.9.5d)
circuit board: 8.46667cm x 5.64444cm
breadboards: 1

parts:
  U1 = NodeMCU V1.0
  DHT1 = DHT11 Humitidy and Temperature Sensor (3 pins)
  OLED1 = OLED 128x64 I2C Monochrome Display

nets:
  N1: U1.D1, OLED1.SCK
  N2: U1.D2, OLED1.SDA
  N3: U1.D3, DHT1.DATA
  3V3: U1.3V3, DHT1.VCC, OLED1.VDD
  GND: U1.GND, DHT1.GND, OLED1.GND

custom parts:
  NodeMCU V1.0: ESP9266 based NodeMCU
  DHT11 Humitidy and Temperature Sensor (3 pins): DHT11 Humidity and Temperature Sensor (3 pins) from the design created by John De Cristofaro for Adafruit Industries.
